# Fritzing sketch arduino_prototype (saved by Fritzing 0.9.3b)
circuit board: 3.84513cm x 4.09089cm
breadboards: 1

parts:
  M1 = DC Motor
  M2 = DC Motor
  IC1 = L293D [package=THT]
  MotorPower = Battery Holders [package=battery-aa-kit]
  U1 = NodeMCU V1.0
  5v = Battery Holders [package=battery-aa-kit]
  J5 = female pin header, 8 pins [form="♀ (female)"]
  J6 = Screw terminal - 2 pins [package=THT]
  J7 = Screw terminal - 2 pins [package=THT]
  J8 = Screw terminal - 2 pins [package=THT]

nets:
  N1: M1.pin_1, IC1.Out_4_(_Controlled_by_Enable_2_), J8.pin1
  N2: M1.pin_2, IC1.Out_3_(_Controlled_by_Enable_2_), J8.pin2
  N3: M2.pin_1, IC1.Out_2_(_Controlled_by_Enable_1_), J7.pin1
  N4: M2.pin_2, IC1.Out_1_(_Controlled_by_Enable_1_), J7.pin2
  N5: IC1.Enable_1, U1.D5, J5.pin6
  N6: IC1.In_1, U1.D6, J5.pin7
  N7: IC1.0V, MotorPower.-, U1.GND, 5v.-, J5.pin5, J6.pin1
  N8: IC1.In_2, U1.D8, J5.pin8
  N9: IC1.+Vmotor, MotorPower.+, J6.pin2
  N10: IC1.Enable_2, U1.D2, J5.pin2
  N11: IC1.In_3, U1.D1, J5.pin1
  N12: IC1.In_4, U1.D4, J5.pin3
  N13: IC1.+V, 5v.+, J5.pin4

custom parts:
  NodeMCU V1.0: ESP8266 based NodeMCU
