# Fritzing sketch esp32cam+led+button+servo+flash (saved by Fritzing 0.9.9b)
circuit board: 2.83304cm x 3.31089cm
circuit board: 4.05088cm x 3.07091cm
circuit board: 2.79354cm x 2.30046cm
circuit board: 3.32608cm x 3.04855cm
breadboards: 2

parts:
  L3 = smd LED [color="Red (633nm)" package="0805 [SMD]"]
  L2 = smd LED [color="Red (633nm)" package="0805 [SMD]"]
  L0 = smd LED [color="Red (633nm)" package="0805 [SMD]"]
  l1 = smd LED [color="Red (633nm)" package="0805 [SMD]"]
  Mod5 = ESP32 - CAM
  VCC5 = Battery
  Button = Pushbutton [package="[THT]"]
  IC5 = L293D [package=THT]
  M0 = DC Motor
  M1 = DC Motor
  J18 = female pin header, 2 pins [form="♀ (female)"]
  J20 = female pin header, 2 pins [form="♀ (female)"]
  J21 = female pin header, 8 pins [form="♀ (female)"]
  J22 = female pin header, 2 pins [form="♀ (female)"]
  J23 = female pin header, 2 pins [form="♀ (female)"]
  J24 = female pin header, 3 pins [form="♀ (female)"]
  J25 = female pin header, 2 pins [form="♀ (female)"]
  J26 = male pin header, 6 pins [form="♂ (male)"]
  J27 = female pin header, 2 pins [form="♀ (female)"]
  J29 = female pin header, 8 pins [form="♀ (female)"]
  J19 = female pin header, 3 pins [form="♀ (female)"]
  M14 = RioRand LM2596
  J17 = male pin header, 7 pins [form="♂ (male)"]
  Mod6 = ESP32 - CAM
  J32 = female pin header, 6 pins [form="♀ (female)"]
  Part2 = FTDI Basic Programmer
  J33 = female pin header, 8 pins [form="♀ (female)"]
  J34 = female pin header, 8 pins [form="♀ (female)"]
  J30 = male pin header, 8 pins [form="♂ (male)"]
  J28 = male pin header, 8 pins [form="♂ (male)"]
  Mod7 = ESP32 - CAM  # not connected

nets:
  N1: L3.cathode, L2.cathode, L0.cathode, l1.cathode, Mod5.GND, Mod5.IO2, Button.Pin_1, Button.Pin_2, IC5.0V, J18.pin2, J20.pin1, J21.pin4, J21.pin8, J23.pin1, J24.pin3, J26.pin3, J26.pin6, J27.pin1, J29.pin2, J29.pin7, J19.pin3, M14.Pin_4, J17.pin4, J30.pin2, J30.pin7, J28.pin4, J28.pin8
  N2: L3.anode, Mod5.IO12, J26.pin1, J27.pin2, J29.pin3, J30.pin3
  N3: L2.anode, Mod5.IO14, J20.pin2, J26.pin5, J29.pin6, J30.pin6
  N4: L0.anode, Mod5.IO15, J23.pin2, J26.pin4, J29.pin5, J30.pin5
  N5: l1.anode, Mod5.IO13, J18.pin1, J26.pin2, J29.pin4, J30.pin4
  N6: Mod5.5V, J29.pin1, M14.Pin_3, J30.pin1
  N7: Mod5.IO4, IC5.Enable_1, IC5.Enable_2, J29.pin8, J17.pin5, J30.pin8
  N8: Mod5.VOT, IC5.In_3, J21.pin7, J17.pin1, J28.pin7
  N9: Mod5.VOR, IC5.In_4, J21.pin6, J17.pin2, J28.pin6
  N10: Mod5.VCC, IC5.+Vmotor, IC5.+V, J21.pin5, J17.pin3, J28.pin5
  N11: Mod5.IO0, IC5.In_1, J21.pin3, J17.pin6, J28.pin3
  N12: VCC5.-, M14.Pin_2
  N13: VCC5.+, M14.Pin_1
  N14: Button.Pin_3, Button.Pin_4, J24.pin1, J19.pin1
  N15: IC5.Out_1_(_Controlled_by_Enable_1_), M1.pin_2, J22.pin2
  N16: IC5.Out_2_(_Controlled_by_Enable_1_), M1.pin_1, J22.pin1
  N17: IC5.In_2, J21.pin2, J17.pin7, J28.pin2
  N18: IC5.Out_3_(_Controlled_by_Enable_2_), M0.pin_1, J25.pin1
  N19: IC5.Out_4_(_Controlled_by_Enable_2_), M0.pin_2, J25.pin2
  N20: J21.pin1, J28.pin1
  N21: Mod6.5V, J32.pin4, Part2.POWER, J34.pin1
  GND: Mod6.GND, J32.pin6, Part2.GND, J33.pin8
  N22: Mod6.VOT, J32.pin2, Part2.RXI, J33.pin7
  N23: Mod6.VOR, J32.pin3, Part2.TXO, J33.pin6
  N24: J33.pin3, J33.pin4

notes:
  2
  3
  5
  9
  4
  12
  15
  14
  13

custom parts:
  ESP32 - CAM: The ESP32-CAM has a very competitive small-size camera module that can operate independently as a minimum system with a footprint of only 27*40.5*4.5mm and a deep sleep current of up to 6mA.
